// Logisim project CPU.circ as structural Verilog
// REGS
module RegisterBank (
  input  [15:0] DATA_IN,
  input  CHIP_ENABLE,
  input  ZERO_ENABLE,
  input  [2:0] ADDR,
  input  READ_WRITE,
  output [15:0] DATA_OUT
);

  wire clock_1_out, decoder_1_out0, decoder_1_out1, decoder_1_out2, decoder_1_out3, decoder_1_out4,
       decoder_1_out5, decoder_1_out6, decoder_1_out7, not_1_out;
  wire [15:0] controlled_buffer_1_out, controlled_buffer_2_out, multiplexer_1_out, Reg0_q, Reg1_q, Reg2_q,
       Reg3_q, Reg4_q, Reg5_q, Reg6_q, Reg7_q;

  Clock clock_1 (.out(clock_1_out));
  Pull_Resistor pull_resistor_1 (.node(READ_WRITE));
  Decoder #(.select(3), .disabled(0)) decoder_1 (
    .out0(decoder_1_out0), .out1(decoder_1_out1), .out2(decoder_1_out2), .out3(decoder_1_out3),
    .out4(decoder_1_out4), .out5(decoder_1_out5), .out6(decoder_1_out6), .out7(decoder_1_out7), .sel(ADDR),
    .en(READ_WRITE));
  assign controlled_buffer_1_out = CHIP_ENABLE ? DATA_IN : 16'bz;  // Controlled_Buffer controlled_buffer_1
  not not_1 (not_1_out, READ_WRITE);
  assign controlled_buffer_2_out = READ_WRITE ? controlled_buffer_1_out : 16'bz;  // Controlled_Buffer controlled_buffer_2
  Register #(.width(16), .trigger("high")) Reg0 (
    .D(controlled_buffer_2_out), .en(decoder_1_out0), .Q(Reg0_q), .clk(clock_1_out), .clr(ZERO_ENABLE));
  Register #(.width(16), .trigger("high")) Reg1 (
    .D(controlled_buffer_2_out), .en(decoder_1_out1), .Q(Reg1_q), .clk(clock_1_out));  // open: clr
  Register #(.width(16), .trigger("high")) Reg2 (
    .D(controlled_buffer_2_out), .en(decoder_1_out2), .Q(Reg2_q), .clk(clock_1_out));  // open: clr
  Register #(.width(16), .trigger("high")) Reg3 (
    .D(controlled_buffer_2_out), .en(decoder_1_out3), .Q(Reg3_q), .clk(clock_1_out));  // open: clr
  Register #(.width(16), .trigger("high")) Reg4 (
    .D(controlled_buffer_2_out), .en(decoder_1_out4), .Q(Reg4_q), .clk(clock_1_out));  // open: clr
  Register #(.width(16), .trigger("high")) Reg5 (
    .D(controlled_buffer_2_out), .en(decoder_1_out5), .Q(Reg5_q), .clk(clock_1_out));  // open: clr
  Register #(.width(16), .trigger("high")) Reg6 (
    .D(controlled_buffer_2_out), .en(decoder_1_out6), .Q(Reg6_q), .clk(clock_1_out));  // open: clr
  Register #(.width(16), .trigger("high")) Reg7 (
    .D(controlled_buffer_2_out), .en(decoder_1_out7), .Q(Reg7_q), .clk(clock_1_out));  // open: clr
  Pull_Resistor pull_resistor_2 (.node(not_1_out));
  Multiplexer #(.select(3), .width(16)) multiplexer_1 (
    .in0(Reg0_q), .in1(Reg1_q), .in2(Reg2_q), .in3(Reg3_q), .in4(Reg4_q), .in5(Reg5_q), .in6(Reg6_q),
    .in7(Reg7_q), .out(multiplexer_1_out), .sel(ADDR), .en(not_1_out));
  assign DATA_OUT = CHIP_ENABLE ? multiplexer_1_out : 16'bz;  // Controlled_Buffer controlled_buffer_3

  // Notes on the sheet:
  //   DATA_IN: pull=down
  //   ADDR: pull=down
endmodule

module ALU (
  input  [2:0] OPCODE_IN,
  input  READ_WRITE,
  input  [15:0] DATA_IN,
  input  ADDR,
  input  CHIP_ENABLE,
  output [15:0] DATA_OUT,
  output REGA___REGB,
  output REGA___REGB_2,
  output REGA___REGB_3
);

  wire button_1_out, button_2_out, clock_1_out, decoder_1_out0, decoder_1_out1, not_1_out;
  wire [15:0] adder_1_out, controlled_buffer_1_out, controlled_buffer_2_out, multiplexer_1_out, nand_1_out,
       RegA_q, RegB_q;

  Button button_1 (.out(button_1_out));
  Decoder #(.disabled(0)) decoder_1 (.out0(decoder_1_out0), .out1(decoder_1_out1), .sel(ADDR), .en(READ_WRITE));
  Button button_2 (.out(button_2_out));
  assign controlled_buffer_1_out = CHIP_ENABLE ? DATA_IN : 16'bz;  // Controlled_Buffer controlled_buffer_1
  assign controlled_buffer_2_out = READ_WRITE ? controlled_buffer_1_out : 16'bz;  // Controlled_Buffer controlled_buffer_2
  Register #(.width(16), .trigger("high")) RegA (
    .D(controlled_buffer_2_out), .en(decoder_1_out0), .Q(RegA_q), .clk(clock_1_out), .clr(button_1_out));
  Clock clock_1 (.out(clock_1_out));
  Register #(.width(16), .trigger("high")) RegB (
    .D(controlled_buffer_2_out), .en(decoder_1_out1), .Q(RegB_q), .clk(clock_1_out), .clr(button_2_out));
  Adder #(.width(16)) adder_1 (.a(RegA_q), .b(RegB_q), .out(adder_1_out));  // open: cin, cout
  assign nand_1_out = ~(RegA_q & RegB_q);  // NAND_Gate nand_1, 16 bits wide
  Comparator #(.width(16)) comparator_1 (
    .a(RegA_q), .b(RegB_q), .gt(REGA___REGB), .eq(REGA___REGB_2), .lt(REGA___REGB_3));
  not not_1 (not_1_out, READ_WRITE);
  Multiplexer #(.select(3), .width(16)) multiplexer_1 (
    .in0(adder_1_out), .in1(adder_1_out), .in2(nand_1_out), .out(multiplexer_1_out), .sel(OPCODE_IN),
    .en(not_1_out));  // open: in3, in4, in5, in6, in7
  assign DATA_OUT = CHIP_ENABLE ? multiplexer_1_out : 16'bz;  // Controlled_Buffer controlled_buffer_3

  // Notes on the sheet:
  //   CHIP_ENABLE: pull=down
  //   DATA_IN: pull=down
  //   REGA___REGB_3: pull=down
  //   REGA___REGB: pull=down
  //   REGA___REGB_2: pull=down
endmodule

module CPU (
  input  [15:0] DATA_IN,
  output BUS_R_W,
  output [15:0] DATA_OUT,
  output [15:0] ADDRESS_BUS
);

  wire _CLK, A_B, A_B_t, A_B_t_t, ADDR_REG_A_W, ADDR_REG_B_W, ADDR_REG_W_ENABLE, ALU_ENABLE, ALU_R_S,
       ALU_R_W, BUS_ENABLE, CLK, controlled_buffer_8_out, controlled_buffer_9_out, ENA_R_0, ENA_R_1, ENA_R_A,
       ENA_R_B, ENA_R_C, IMM_ENABLE, INSTR_REG_R_W, INSTR_REG_WE, MPG_RST, NOP, not_1_out, not_2_out,
       not_4_out, PC_ENABLE, PGC_INC, PGC_L, PGC_OVF, pull_resistor_17_node, REG_ENABLE, REG_R_W, SEL_RW_0,
       SEL_RW_1, SEL_RW_2;
  wire [1:0] MPG_ADDR;
  wire [2:0] REG_ADDR;
  wire [6:0] bit_extender_2_out, IMM_7;
  wire [9:7] IMM_10;
  wire [13:12] rom_2_data;
  wire [15:0] adder_1_out, bit_extender_1_out, controlled_buffer_6_out, controlled_buffer_7_out,
       controlled_buffer_10_out, controlled_buffer_11_out, counter_2_q, DATA_BUS, PGC;
  wire [15:10] INSTRUCTION;

  RegisterBank RB1 (
    .DATA_IN(DATA_BUS), .DATA_OUT(DATA_BUS), .READ_WRITE(REG_R_W), .ADDR(REG_ADDR), .CHIP_ENABLE(REG_ENABLE),
    .ZERO_ENABLE(1'b1));
  // Probe on INSTRUCTION[12:10]
  assign REG_ADDR = ENA_R_A ? INSTRUCTION[12:10] : 3'bz;  // Controlled_Buffer controlled_buffer_1
  // Probe on IMM_10
  assign REG_ADDR = ENA_R_B ? IMM_10 : 3'bz;  // Controlled_Buffer controlled_buffer_2
  // Probe on IMM_7[2:0]
  assign REG_ADDR = ENA_R_C ? IMM_7[2:0] : 3'bz;  // Controlled_Buffer controlled_buffer_3
  // Probe on INSTRUCTION[15:13]
  // Probe on INSTRUCTION[12:10]
  // Probe on IMM_7
  // Probe on {IMM_10, IMM_7}
  ALU alu_1 (
    .DATA_IN(DATA_BUS), .DATA_OUT(DATA_BUS), .REGA___REGB_2(A_B_t), .ADDR(ALU_R_S), .READ_WRITE(ALU_R_W),
    .OPCODE_IN(INSTRUCTION[15:13]), .CHIP_ENABLE(ALU_ENABLE), .REGA___REGB(A_B_t_t), .REGA___REGB_3(A_B));
  // Probe on DATA_BUS
  // Probe on IMM_10
  // Probe on IMM_7[2:0]
  Decoder #(.select(3), .disabled(0), .enable("false")) decoder_1 (
    .out1(REG_R_W), .out2(ALU_R_W), .out3(BUS_R_W), .out4(PGC_L), .out5(INSTR_REG_R_W), .out6(ADDR_REG_A_W),
    .out7(ADDR_REG_B_W), .sel({SEL_RW_2, SEL_RW_1, SEL_RW_0}));  // open: out0
  // Probe on ADDRESS_BUS
  not not_1 (not_1_out, BUS_R_W);
  assign DATA_OUT = BUS_R_W ? controlled_buffer_7_out : 16'bz;  // Controlled_Buffer controlled_buffer_4
  assign DATA_BUS = BUS_ENABLE ? controlled_buffer_6_out : 16'bz;  // Controlled_Buffer controlled_buffer_5
  assign controlled_buffer_6_out = not_1_out ? DATA_IN : 16'bz;  // Controlled_Buffer controlled_buffer_6
  assign controlled_buffer_7_out = BUS_ENABLE ? DATA_BUS : 16'bz;  // Controlled_Buffer controlled_buffer_7
  ROM #(.addrWidth(16), .dataWidth(16)) rom_1 (.addr(ADDRESS_BUS), .data(DATA_BUS), .sel(PGC_INC));
  Decoder #(.select(2), .disabled(0), .enable("false")) decoder_2 (
    .out1(ENA_R_A), .out2(ENA_R_B), .out3(ENA_R_C), .sel({ENA_R_1, ENA_R_0}));  // open: out0
  // IMM_CONTROLLER IMM_CON: pin names not known; wires that end beside it: DATA_BUS, INSTRUCTION[15:13], IMM_ENABLE, {IMM_10, IMM_7}, IMM_7
  nor nor_1 (NOP, IMM_7[0], IMM_7[1], IMM_7[2], IMM_7[3], IMM_7[4], IMM_7[5], IMM_7[6], IMM_10[7], IMM_10[8], IMM_10[9], INSTRUCTION[10], INSTRUCTION[11], INSTRUCTION[12], INSTRUCTION[13], INSTRUCTION[14], INSTRUCTION[15]);
  // Probe on DATA_BUS
  or or_1 (REG_ENABLE, ENA_R_0, ENA_R_1);
  // Probe on MPG_ADDR
  Counter #(.width(2), .max('h3), .trigger("falling")) counter_1 (
    .Q(MPG_ADDR), .clk(CLK), .clr(controlled_buffer_8_out));  // open: load, D, count, carry
  assign controlled_buffer_8_out = CLK ? MPG_RST : 1'bz;  // Controlled_Buffer controlled_buffer_8
  // Probe on INSTRUCTION[15:13]
  not not_2 (not_2_out, NOP);
  Pull_Resistor pull_resistor_1 (.node(SEL_RW_0));
  Pull_Resistor pull_resistor_2 (.node(ENA_R_0));
  Pull_Resistor pull_resistor_3 (.node(ALU_ENABLE));
  ROM #(.addrWidth(5), .dataWidth(16)) rom_2 (
    .addr({INSTRUCTION[15:13], MPG_ADDR}),
    .data({MPG_RST, PGC_INC, rom_2_data, ADDR_REG_W_ENABLE, IMM_ENABLE, INSTR_REG_WE, PC_ENABLE, BUS_ENABLE, ALU_ENABLE, ALU_R_S, ENA_R_1, ENA_R_0, SEL_RW_2, SEL_RW_1, SEL_RW_0}),
    .sel(not_2_out));
  Pull_Resistor pull_resistor_4 (.node(INSTR_REG_WE));
  Pull_Resistor pull_resistor_5 (.node(rom_2_data[12]));
  Pull_Resistor pull_resistor_6 (.node(MPG_RST));
  Pull_Resistor pull_resistor_7 (.node(SEL_RW_1));
  Pull_Resistor pull_resistor_8 (.node(SEL_RW_2));
  Pull_Resistor pull_resistor_9 (.node(ENA_R_1));
  Pull_Resistor pull_resistor_10 (.node(ALU_R_S));
  Pull_Resistor pull_resistor_11 (.node(BUS_ENABLE));
  Pull_Resistor pull_resistor_12 (.node(PC_ENABLE));
  Pull_Resistor pull_resistor_13 (.node(IMM_ENABLE));
  Pull_Resistor pull_resistor_14 (.node(ADDR_REG_W_ENABLE));
  Pull_Resistor pull_resistor_15 (.node(rom_2_data[13]));
  Pull_Resistor pull_resistor_16 (.node(PGC_INC));
  not not_3 (_CLK, CLK);
  Clock clock_1 (.out(CLK));
  // Probe on DATA_BUS
  // Probe on PGC
  Controlled_Buffer controlled_buffer_9 (.out(controlled_buffer_9_out));  // open: in, en
  ADDR_REG addr_reg_1 (
    .ADDRESS(ADDRESS_BUS), .DATA(DATA_BUS), .REG_A_SELECT(ADDR_REG_A_W), .REG_WE(ADDR_REG_W_ENABLE),
    .OE(BUS_ENABLE), .CLK(CLK), .REG_B_SELECT(ADDR_REG_B_W));
  and and_1 (PGC_L, INSTRUCTION[15], INSTRUCTION[14], ~INSTRUCTION[13], A_B_t, MPG_ADDR[1], ~MPG_ADDR[0]);  // AND_Gate
  // Probe on DATA_BUS
  assign controlled_buffer_10_out = PGC_L ? DATA_BUS : 16'bz;  // Controlled_Buffer controlled_buffer_10
  assign controlled_buffer_11_out = PGC_L ? PGC : 16'bz;  // Controlled_Buffer controlled_buffer_11
  Register #(.width(16), .trigger("high")) register_1 (
    .D(DATA_BUS), .en(INSTR_REG_WE), .Q({INSTRUCTION, IMM_10, IMM_7}), .clk(CLK));  // open: clr
  // Probe on {INSTRUCTION, IMM_10, IMM_7}
  not not_4 (not_4_out, PGC_L);
  assign PGC = not_4_out ? counter_2_q : 16'bz;  // Controlled_Buffer controlled_buffer_12
  Counter #(.width(16), .max('hffff), .ongoal("load"), .trigger("falling")) counter_2 (
    .load(PGC_L), .count(controlled_buffer_9_out), .Q(counter_2_q), .carry(PGC_OVF), .clk(CLK));  // open: D, clr
  assign bit_extender_1_out = {{9{bit_extender_2_out[6]}}, bit_extender_2_out};  // Bit_Extender bit_extender_1
  Bit_Extender #(.in_width(16), .out_width(7)) bit_extender_2 (.in(controlled_buffer_10_out), .out(bit_extender_2_out));
  // Probe on controlled_buffer_11_out
  Pull_Resistor #(.pull(1)) pull_resistor_17 (.node(pull_resistor_17_node));
  Adder #(.width(16)) adder_1 (
    .a(bit_extender_1_out), .b(controlled_buffer_11_out), .out(adder_1_out), .cin(pull_resistor_17_node));  // open: cout
  // Probe on adder_1_out

  // Other names for the same wires on the sheet: IMM_10[6:0] = IMM_7; INSTRUCTION[9:0] = {IMM_10, IMM_7};
  //   RegC[2:0] = IMM_7[2:0]; RegB[2:0] = IMM_10; RegA[2:0] = INSTRUCTION[12:10]; MPG_CTR[1:0] = MPG_ADDR;
  //   MPG_ADDR[4:2] = INSTRUCTION[15:13]; OPCODE[2:0] = INSTRUCTION[15:13]; PGC_W = PGC_L

  // Notes on the sheet:
  //   BUS_R_W: pull=down
  //   DATA_IN: pull=down
endmodule

module Computer (
);

  wire [15:0] ADDRESS_BUS, DATA_BUS;

  // CPU cpu_1: pin names not known; wires that end beside it: DATA_BUS, DATA_BUS, ADDRESS_BUS
endmodule

module ADDR_REG (
  input  [15:0] DATA,
  input  REG_A_SELECT,
  input  REG_B_SELECT,
  input  REG_WE,
  input  OE,
  input  CLK,
  output [15:0] ADDRESS
);

  wire controlled_buffer_1_out, controlled_buffer_2_out;
  wire [15:0] adder_1_out, register_1_q, register_2_q;

  assign controlled_buffer_1_out = REG_A_SELECT ? REG_WE : 1'bz;  // Controlled_Buffer controlled_buffer_1
  Pull_Resistor pull_resistor_1 (.node(controlled_buffer_1_out));
  assign controlled_buffer_2_out = REG_B_SELECT ? REG_WE : 1'bz;  // Controlled_Buffer controlled_buffer_2
  Pull_Resistor pull_resistor_2 (.node(controlled_buffer_2_out));
  Register #(.width(16), .trigger("high")) register_1 (
    .D(DATA), .en(controlled_buffer_1_out), .Q(register_1_q), .clk(CLK));  // open: clr
  Register #(.width(16), .trigger("high")) register_2 (
    .D(DATA), .en(controlled_buffer_2_out), .Q(register_2_q), .clk(CLK));  // open: clr
  assign ADDRESS = OE ? adder_1_out : 16'bz;  // Controlled_Buffer controlled_buffer_3
  Adder #(.width(16)) adder_1 (.a(register_1_q), .b(register_2_q), .out(adder_1_out));  // open: cin, cout
  // Probe on ADDRESS
  // Probe on DATA

  // Other names for the same wires on the sheet: ADDR_REG_A = REG_A_SELECT; ADDR_REG_B = REG_B_SELECT;
  //   ADDR_REG_WE = REG_WE; ADDRESS_BUS[15:0] = ADDRESS; DATA_BUS[15:0] = DATA; OUTPUT_ENABLE = OE

  // Notes on the sheet:
  //   REG_WE: pull=down
  //   REG_B_SELECT: pull=down
  //   ADDRESS: pull=down
  //   CLK: pull=down
  //   REG_A_SELECT: pull=down
  //   DATA: pull=down
  //   OE: pull=down
endmodule

// IMM_CTL
module IMM_CONTROLLER (
  input  [2:0] OPCODE,
  input  [9:0] IMM_10,
  input  [6:0] IMM_7,
  output [15:0] DATA_BUS
);

  wire ADDI, BEQ, IMM_7_ENABLE, IMM_10_ENABLE, LW, SW;
  wire [7:0] decoder_1_out0;

  assign DATA_BUS = IMM_10_ENABLE ? {IMM_10, {6{1'b0}}} : 16'bz;  // Controlled_Buffer controlled_buffer_1
  assign DATA_BUS = IMM_7_ENABLE ? {{9{1'b0}}, IMM_7} : 16'bz;  // Controlled_Buffer controlled_buffer_2
  Decoder #(.select(3), .disabled(0), .enable("false")) decoder_1 (
    .out0(decoder_1_out0[0]), .out1(ADDI), .out2(decoder_1_out0[2]), .out3(IMM_10_ENABLE), .out4(SW),
    .out5(LW), .out6(BEQ), .out7(decoder_1_out0[7]), .sel(OPCODE));
  or or_1 (IMM_7_ENABLE, ADDI, SW, LW, BEQ);

  // Other names for the same wires on the sheet: LUI = IMM_10_ENABLE

  // Notes on the sheet:
  //   DATA_BUS: pull=down
  //   OPCODE: pull=down
  //   IMM_10: pull=down
  //   IMM_7: pull=down
endmodule

// REGS
module REGS16_32 (
  input  [3:0] REG_A_ADDR,
  input  [3:0] REG_B_ADDR,
  input  [3:0] REG_C_ADDR,
  input  [3:0] REG_D_ADDR,
  input  _0_ENA,
  input  CLK,
  input  A_ENA,
  input  A_WE,
  input  [31:0] A_IN,
  input  B_ENA,
  input  B_WE,
  input  [31:0] B_IN,
  input  C_ENA,
  input  C_WE,
  input  [31:0] C_IN,
  input  D_ENA,
  input  D_WE,
  input  [31:0] D_IN,
  output [31:0] A_OUT,
  output [31:0] B_OUT,
  output [31:0] C_OUT,
  output [31:0] D_OUT
);

  wire A_0, A_1, A_2, A_3, A_4, A_5, A_6, A_7, A_8, A_9, A_A, A_B, A_C, A_D, A_E, A_F, and_5_out, and_6_out,
       and_7_out, and_8_out, B_0, B_1, B_2, B_3, B_4, B_5, B_6, B_7, B_8, B_9, B_A, B_B, B_C, B_D, B_E, B_F,
       C_0, C_1, C_2, C_3, C_4, C_5, C_6, C_7, C_8, C_9, C_A, C_B, C_C, C_D, C_E, C_F, D_0, D_1, D_2, D_3,
       D_4, D_5, D_6, D_7, D_8, D_9, D_A, D_B, D_C, D_D, D_E, D_F, or_2_out;
  wire [1:0] controlled_buffer_1_out, controlled_buffer_2_out, controlled_buffer_4_out, or_1_out,
       pull_resistor_3_node;
  wire [3:0] and_1_out;
  wire [31:0] multiplexer_1_out, register_1_q;

  Decoder #(.select(4), .disabled(0)) decoder_1 (
    .out0(A_0), .out1(A_1), .out2(A_2), .out3(A_3), .out4(A_4), .out5(A_5), .out6(A_6), .out7(A_7),
    .out8(A_8), .out9(A_9), .out10(A_A), .out11(A_B), .out12(A_C), .out13(A_D), .out14(A_E), .out15(A_F),
    .sel(REG_A_ADDR), .en(A_ENA));
  Decoder #(.select(4), .disabled(0)) decoder_2 (
    .out0(B_0), .out1(B_1), .out2(B_2), .out3(B_3), .out4(B_4), .out5(B_5), .out6(B_6), .out7(B_7),
    .out8(B_8), .out9(B_9), .out10(B_A), .out11(B_B), .out12(B_C), .out13(B_D), .out14(B_E), .out15(B_F),
    .sel(REG_B_ADDR), .en(B_ENA));
  Decoder #(.select(4), .disabled(0)) decoder_3 (
    .out0(C_0), .out1(C_1), .out2(C_2), .out3(C_3), .out4(C_4), .out5(C_5), .out6(C_6), .out7(C_7),
    .out8(C_8), .out9(C_9), .out10(C_A), .out11(C_B), .out12(C_C), .out13(C_D), .out14(C_E), .out15(C_F),
    .sel(REG_C_ADDR), .en(C_ENA));
  Decoder #(.select(4), .disabled(0)) decoder_4 (
    .out0(D_0), .out1(D_1), .out2(D_2), .out3(D_3), .out4(D_4), .out5(D_5), .out6(D_6), .out7(D_7),
    .out8(D_8), .out9(D_9), .out10(D_A), .out11(D_B), .out12(D_C), .out13(D_D), .out14(D_E), .out15(D_F),
    .sel(REG_D_ADDR), .en(D_ENA));
  buf and_1 (and_1_out[0], A_0);  // AND_Gate
  buf and_2 (and_1_out[1], B_0);  // AND_Gate
  buf and_3 (and_1_out[2], C_0);  // AND_Gate
  buf and_4 (and_1_out[3], D_0);  // AND_Gate
  assign controlled_buffer_1_out = and_1_out[0] ? 2'b00 : 2'bz;  // Controlled_Buffer controlled_buffer_1
  Pull_Resistor pull_resistor_1 (.node(controlled_buffer_1_out));
  assign controlled_buffer_2_out = and_1_out[1] ? 2'b01 : 2'bz;  // Controlled_Buffer controlled_buffer_2
  Pull_Resistor pull_resistor_2 (.node(controlled_buffer_2_out));
  Pull_Resistor pull_resistor_3 (.node(pull_resistor_3_node));
  assign pull_resistor_3_node = and_1_out[2] ? 2'b10 : 2'bz;  // Controlled_Buffer controlled_buffer_3
  assign controlled_buffer_4_out = and_1_out[3] ? 2'b11 : 2'bz;  // Controlled_Buffer controlled_buffer_4
  Pull_Resistor pull_resistor_4 (.node(controlled_buffer_4_out));
  assign or_1_out = controlled_buffer_1_out | controlled_buffer_2_out | pull_resistor_3_node | controlled_buffer_4_out;  // OR_Gate or_1, 2 bits wide
  Multiplexer #(.select(2), .width(32), .disabled(0), .enable("false")) multiplexer_1 (
    .in0(A_IN), .in1(B_IN), .in2(C_IN), .in3(D_IN), .out(multiplexer_1_out), .sel(or_1_out));
  or or_2 (or_2_out, and_1_out[0], and_1_out[1], and_1_out[2], and_1_out[3]);
  and and_5 (and_5_out, A_0, ~A_WE);  // AND_Gate
  Register #(.width(32)) register_1 (.D(multiplexer_1_out), .en(or_2_out), .Q(register_1_q), .clk(CLK), .clr(_0_ENA));
  assign A_OUT = and_5_out ? register_1_q : 32'bz;  // Controlled_Buffer controlled_buffer_5
  and and_6 (and_6_out, C_0, ~C_WE);  // AND_Gate
  and and_7 (and_7_out, B_0, ~B_WE);  // AND_Gate
  assign B_OUT = and_7_out ? register_1_q : 32'bz;  // Controlled_Buffer controlled_buffer_6
  assign C_OUT = and_6_out ? register_1_q : 32'bz;  // Controlled_Buffer controlled_buffer_7
  and and_8 (and_8_out, D_0, ~D_WE);  // AND_Gate
  assign D_OUT = and_8_out ? register_1_q : 32'bz;  // Controlled_Buffer controlled_buffer_8

  // Notes on the sheet:
  //   REG_D_ADDR: pull=down
  //   REG_C_ADDR: pull=down
  //   D_OUT: pull=down
  //   B_ENA: pull=down
  //   D_ENA: pull=down
  //   A_WE: pull=down
  //   REG_A_ADDR: pull=down
  //   D_WE: pull=down
  //   C_WE: pull=down
  //   REG_B_ADDR: pull=down
  //   C_ENA: pull=down
  //   B_WE: pull=down
  //   B_OUT: pull=down
  //   _0_ENA: pull=down
  //   A_OUT: pull=down
  //   C_OUT: pull=down
  //   A_ENA: pull=down
  //   CLK: pull=down
endmodule

module REGS256_32 (
);

  wire A_ENA, A_WE, B_ENA, B_WE, C_ENA, CLK, Transfer, transmission_1_p3;
  wire [3:0] A_ADR_LO, B_ADR_LO, C_ADR_LO;
  wire [31:0] A_DATA, B_DATA, C_DATA;

  // NOT_Gate not_1 has open pins: in=Transfer, out=open
  // Probe on transmission_1_p3
  // Transmission_Gate #(.width(32)) transmission_1: pin names not known; wires that end beside it: {32{1'b1}}, Transfer, transmission_1_p3
  Button button_1 (.out(Transfer));
  REGS16_32 regs16_32_1 (
    .A_ENA(A_ENA), .A_WE(A_WE), .A_IN(A_DATA), .A_OUT(A_DATA), .B_ENA(B_ENA), .B_WE(B_WE), .B_IN(B_DATA),
    .B_OUT(B_DATA), .C_ENA(C_ENA), .C_WE(A_WE), .C_IN(C_DATA), .C_OUT(C_DATA), .REG_A_ADDR(A_ADR_LO),
    .REG_B_ADDR(B_ADR_LO), .REG_C_ADDR(C_ADR_LO), .CLK(CLK), .D_ENA(CLK));  // open: REG_D_ADDR, D_WE, D_IN, D_OUT, _0_ENA
endmodule

module INTERRUPT_STACK (
  input  POP,
  input  PUSH,
  input  ENA,
  input  [31:0] DATA_IN,
  output [31:0] DATA_OUT
);

  wire _1, _2, _3, buffer_3_out, button_1_out, clock_1_out, clock_2_out, DEC, INC, not_1_out, or_1_out, WE;
  wire [0:0] decoder_1_out0;
  wire [15:0] counter_1_q;
  wire [31:0] controlled_buffer_1_out, ram_1_data;

  Pull_Resistor pull_resistor_1 (.node(DEC));
  or or_1 (or_1_out, DEC, INC);
  Clock clock_1 (.out(clock_1_out));
  Button button_1 (.out(button_1_out));
  Pull_Resistor pull_resistor_2 (.node(or_1_out));
  Decoder #(.select(2)) decoder_1 (
    .out0(decoder_1_out0[0]), .out1(_1), .out2(_2), .out3(_3), .sel({PUSH, POP}), .en(ENA));
  Counter #(.width(16), .max('hffff), .ongoal("stay"), .trigger("falling")) counter_1 (
    .load(DEC), .count(or_1_out), .Q(counter_1_q), .clk(clock_1_out), .clr(button_1_out));  // open: D, carry
  assign controlled_buffer_1_out = WE ? DATA_IN : 32'bz;  // Controlled_Buffer controlled_buffer_1
  Pull_Resistor pull_resistor_3 (.node(controlled_buffer_1_out));
  Clock clock_2 (.out(clock_2_out));
  buf buffer_1 (DEC, _1);
  buf buffer_2 (INC, _2);
  Pull_Resistor pull_resistor_4 (.node(_1));
  Pull_Resistor pull_resistor_5 (.node(_2));
  Pull_Resistor pull_resistor_6 (.node(_3));
  buf buffer_3 (buffer_3_out, _3);
  not not_1 (not_1_out, WE);
  RAM #(.addrWidth(16), .dataWidth(32), .bus("separate")) ram_1 (
    .addr(counter_1_q), .din(controlled_buffer_1_out), .data(ram_1_data), .str(WE), .sel(ENA),
    .clk(clock_2_out));  // open: ld, clr
  assign DATA_OUT = not_1_out ? ram_1_data : 32'bz;  // Controlled_Buffer controlled_buffer_2
  or or_2 (WE, _2, buffer_3_out);

  // Notes on the sheet:
  //   ENA: pull=down
  //   POP: pull=down
  //   DATA_OUT: pull=down
  //   PUSH: pull=down
  //   DATA_IN: pull=down
endmodule
